# Fritzing sketch PCB (saved by Fritzing 0.9.3b)
circuit board: 8.59438cm x 4.25793cm
breadboards: 1

parts:
  Q1 = NPN-Transistor [package="TO92 [THT]"]
  C1 = Ceramic Capacitor [capacitance=120pF voltage=35V package="200 mil [THT, multilayer]"]
  U1 = MOC3031-M [package=dil06]
  U2 = TRIAC [package=to-92]
  R2 = Resistor [tolerance=±5% resistance=40 package=THT]
  R3 = Resistor [tolerance=±5% resistance=40 package=THT]
  JP1 = Header 3 [package=jst-3-pth]
  JP2 = Header 3 [package=jst-3-pth]
  JP3 = Header 3 [package=jst-3-pth]
  R4 = Resistor [tolerance=±5% resistance=210k package=THT]
  C2 = Ceramic Capacitor [capacitance=10pF package="100 mil [THT, multilayer]"]
  R5 = Resistor [tolerance=±5% resistance=220 package=THT]

nets:
  N1: Q1.E, JP1.1
  N2: Q1.B, JP1.2
  N3: Q1.C, U1.2
  N4: C1.0, R3.Pin_0
  N5: C1.1, U2.M1, JP3.3, C2.1
  N6: U1.1, R5.Pin_1
  N7: U1.4, U2.G
  N8: U1.6, R2.Pin_0
  N9: U2.M2, R2.Pin_1, R3.Pin_1, JP2.1, R4.Pin_0
  N10: JP1.3, R5.Pin_0
  N11: JP2.3, JP3.2
  N12: R4.Pin_1, C2.0
